# Fritzing sketch Untitled (saved by Fritzing 0.8.7b)
breadboards: 1

parts:
  Q1 = NPN-Transistor [package="TO92 [THT]"]
  R1 = Resistor [tolerance=±5% resistance=220 package=THT]
  LED1 = LED - 5mm [color="Red (633nm)" package="5 mm [THT]"]  # not connected
  R2 = Photocell (LDR) [package=THT]
  R3 = Resistor [tolerance=±5% resistance=220 package=THT]
  Part1 = Arduino Nano (Rev3.0)

nets:
  GND: Q1.E, R3.Pin_1, Part1.GND
  N1: Q1.B, R2.pin_1, R3.Pin_0
  N2: R1.Pin_1, Part1.A0
  5V: R2.pin_0, Part1.5V
